# Fritzing sketch pir1 (saved by Fritzing 0.9.3b)
circuit board: 4.2cm x 4.4cm
breadboards: 1

parts:
  J4 = female pin header, 6 pins [form="♀ (female)"]
  J2 = female pin header, 14 pins [form="♀ (female)"]
  J1 = female pin header, 14 pins [form="♀ (female)"]
  J3 = female pin header, 11 pins [form="♀ (female)"]
  J6 = female pin header, 4 pins [form="♀ (female)"]
  J5 = female pin header, 4 pins [form="♀ (female)"]

nets:
  vin: J4.pin1, J1.pin14, J3.pin10
  gnd: J4.pin3, J1.pin12, J3.pin11, J6.pin1, J6.pin2, J6.pin3, J6.pin4
  sda: J4.pin4, J1.pin8
  scl: J4.pin5, J1.pin7
  N1: J2.pin1, J5.pin1
  N2: J2.pin2, J5.pin2
  N3: J2.pin3, J5.pin3
  rst: J2.pin4, J3.pin4
  oledcs: J2.pin5, J3.pin5
  dc: J2.pin6, J3.pin3
  mosi: J2.pin7, J3.pin1
  sclk: J2.pin9, J3.pin2
  y1: J2.pin14, J5.pin4

notes:
  wbus-dip28
  OLED
  x6
  x5
  x4
  y1
  Gnd
  AMG8833
  Vin
  sda
  scl
  USB
